// Logisim project main3.circ as structural Verilog: 27 circuits, main circuit Calculadora
module ALU_8 (
  input  Cin,
  input  [7:0] A,
  input  [7:0] B,
  input  [2:0] OP,
  output Z,
  output [7:0] S,
  output C
);

  wire add_8_1_overflow__carry_out, mux_4_1_1_1_m, shl_8_1_cout, shr_8_1_cout, sub_8_1_overflow__borrow_out,
       valida_cout_1_s;
  wire [7:0] add_8_1_out_5, and_8_1_out_3, or_8_1_out_3, shl_8_1_shift_left__x2, shr_8_1_shift_right__x1_2,
       sub_8_1_out_5, xor_8_1_out_3;

  ADD_8 add_8_1 (
    .in_1(A), .in_2(B), .OVERFLOW__CARRY_OUT(add_8_1_overflow__carry_out), .out_5(add_8_1_out_5), .Cin(Cin));
  SUB_8 sub_8_1 (
    .in_1(B), .in_2(A), .OVERFLOW__BORROW_OUT(sub_8_1_overflow__borrow_out), .Bin(Cin), .out_5(sub_8_1_out_5));
  XOR_8 xor_8_1 (.in_1(B), .in_2(A), .out_3(xor_8_1_out_3));
  OR_8 or_8_1 (.in_1(B), .in_2(A), .out_3(or_8_1_out_3));
  AND_8 and_8_1 (.in_1(B), .in_2(A), .out_3(and_8_1_out_3));
  SHL_8 shl_8_1 (.SHIFT_LEFT__X2(shl_8_1_shift_left__x2), .in_2(A), .Cout(shl_8_1_cout), .Cin(Cin));
  SHR_8 shr_8_1 (.SHIFT_RIGHT__X1_2(shr_8_1_shift_right__x1_2), .in_1(A), .Cout(shr_8_1_cout), .Cin(Cin));
  MUX_8_1_8 mux_8_1_8_1 (
    .in_1(add_8_1_out_5), .in_2(sub_8_1_out_5), .in_3(xor_8_1_out_3), .in_4(or_8_1_out_3),
    .in_5(and_8_1_out_3), .in_6(shl_8_1_shift_left__x2), .in_7(shr_8_1_shift_right__x1_2), .in_8({8{1'b0}}),
    .M(S), .S1(OP[0]), .S2(OP[1]), .S3(OP[2]));
  ZERO zero_1 (.in_1(S), .Z(Z));
  VALIDA_COUT valida_cout_1 (.A(OP[2]), .B(OP[1]), .C(OP[0]), .S(valida_cout_1_s));
  MUX_4_1_1 mux_4_1_1_1 (
    .in_1(add_8_1_overflow__carry_out), .in_2(sub_8_1_overflow__borrow_out), .in_3(shr_8_1_cout),
    .in_4(shl_8_1_cout), .M(mux_4_1_1_1_m), .in_5(OP[0]), .in_6(OP[2]));
  and and_1 (C, valida_cout_1_s, mux_4_1_1_1_m);
endmodule

module ALU_16 (
  input  Cin,
  input  [7:0] A1,
  input  [7:0] B1,
  input  [7:0] A0,
  input  [7:0] B0,
  input  [2:0] OP,
  output [15:0] out_7,
  output C,
  output Z
);

  wire alu_8_1_c, alu_8_1_z, alu_8_2_c, alu_8_2_z, and_1_out, carry_shr_1_s, not_1_out, valida_cins_1_cout;

  VALIDA_CINS valida_cins_1 (.A0(A0), .OP(OP), .Cout0(alu_8_2_c), .Cin(Cin), .Cout(valida_cins_1_cout));
  ALU_8 alu_8_1 (.A(A1), .B(B1), .Z(alu_8_1_z), .S(out_7[7:0]), .C(alu_8_1_c), .Cin(valida_cins_1_cout), .OP(OP));
  CARRY_SHR carry_shr_1 (.in_1(A1), .S(carry_shr_1_s));
  ALU_8 alu_8_2 (.A(A0), .B(B0), .Z(alu_8_2_z), .S(out_7[15:8]), .C(alu_8_2_c), .Cin(and_1_out), .OP(OP));
  not not_1 (not_1_out, carry_shr_1_s);
  and and_1 (and_1_out, not_1_out, alu_8_1_c);
  and and_2 (Z, alu_8_1_z, alu_8_2_z);
  VALIDA_COUTS valida_couts_1 (.Cout0(alu_8_2_c), .Cout1(alu_8_1_c), .A1(A1), .A0(A0), .OP(OP), .Cout(C));
endmodule

module ADD_1 (
  input  A,
  input  B,
  input  Cin,
  output S,
  output Cout
);

  wire and_1_out, and_2_out, and_3_out, and_4_out, and_5_out, and_6_out, and_7_out, not_1_out, not_2_out,
       not_3_out, not_4_out, not_5_out, not_6_out;

  not not_1 (not_1_out, A);
  not not_2 (not_2_out, B);
  not not_3 (not_3_out, A);
  not not_4 (not_4_out, Cin);
  not not_5 (not_5_out, B);
  not not_6 (not_6_out, Cin);
  and and_1 (and_1_out, B, Cin);
  and and_2 (and_2_out, A, Cin);
  and and_3 (and_3_out, A, B);
  and and_4 (and_4_out, not_1_out, not_2_out, Cin);
  and and_5 (and_5_out, not_3_out, B, not_4_out);
  and and_6 (and_6_out, A, not_5_out, not_6_out);
  and and_7 (and_7_out, A, B, Cin);
  or or_1 (Cout, and_1_out, and_2_out, and_3_out);
  or or_2 (S, and_4_out, and_5_out, and_6_out, and_7_out);
endmodule

module ADD_8 (
  input  [7:0] in_1,
  input  [7:0] in_2,
  input  Cin,
  output OVERFLOW__CARRY_OUT,
  output [7:0] out_5
);

  wire add_1_2_cout, add_1_3_cout, add_1_4_cout, add_1_5_cout, add_1_6_cout, add_1_7_cout, add_1_8_cout;

  ADD_1 add_1_1 (.A(in_2[7]), .B(in_1[7]), .Cin(add_1_2_cout), .S(out_5[7]), .Cout(OVERFLOW__CARRY_OUT));
  ADD_1 add_1_2 (.A(in_2[6]), .B(in_1[6]), .Cin(add_1_3_cout), .S(out_5[6]), .Cout(add_1_2_cout));
  ADD_1 add_1_3 (.A(in_2[5]), .B(in_1[5]), .Cin(add_1_4_cout), .S(out_5[5]), .Cout(add_1_3_cout));
  ADD_1 add_1_4 (.A(in_2[4]), .B(in_1[4]), .Cin(add_1_5_cout), .S(out_5[4]), .Cout(add_1_4_cout));
  ADD_1 add_1_5 (.A(in_2[3]), .B(in_1[3]), .Cin(add_1_6_cout), .S(out_5[3]), .Cout(add_1_5_cout));
  ADD_1 add_1_6 (.A(in_2[2]), .B(in_1[2]), .Cin(add_1_7_cout), .S(out_5[2]), .Cout(add_1_6_cout));
  ADD_1 add_1_7 (.A(in_2[1]), .B(in_1[1]), .Cin(add_1_8_cout), .S(out_5[1]), .Cout(add_1_7_cout));
  ADD_1 add_1_8 (.A(in_2[0]), .B(in_1[0]), .Cin(Cin), .S(out_5[0]), .Cout(add_1_8_cout));
endmodule

module SUB_1 (
  input  A,
  input  B,
  input  Bin,
  output S,
  output Bout
);

  wire and_1_out, and_2_out, and_3_out, and_4_out, and_5_out, and_6_out, and_7_out, not_1_out, not_2_out,
       not_3_out, not_4_out, not_5_out, not_6_out, not_7_out, not_8_out;

  not not_1 (not_1_out, A);
  not not_2 (not_2_out, B);
  not not_3 (not_3_out, A);
  not not_4 (not_4_out, Bin);
  not not_5 (not_5_out, B);
  not not_6 (not_6_out, Bin);
  not not_7 (not_7_out, A);
  not not_8 (not_8_out, A);
  and and_1 (and_1_out, not_1_out, not_2_out, Bin);
  and and_2 (and_2_out, not_3_out, B, not_4_out);
  and and_3 (and_3_out, A, not_5_out, not_6_out);
  and and_4 (and_4_out, A, B, Bin);
  and and_5 (and_5_out, not_7_out, Bin);
  and and_6 (and_6_out, not_8_out, B);
  and and_7 (and_7_out, B, Bin);
  or or_1 (S, and_1_out, and_2_out, and_3_out, and_4_out);
  or or_2 (Bout, and_5_out, and_6_out, and_7_out);
endmodule

module SUB_8 (
  input  [7:0] in_1,
  input  [7:0] in_2,
  input  Bin,
  output OVERFLOW__BORROW_OUT,
  output [7:0] out_5
);

  wire sub_1_2_bout, sub_1_3_bout, sub_1_4_bout, sub_1_5_bout, sub_1_6_bout, sub_1_7_bout, sub_1_8_bout;

  SUB_1 sub_1_1 (.A(in_2[7]), .B(in_1[7]), .Bin(sub_1_2_bout), .S(out_5[7]), .Bout(OVERFLOW__BORROW_OUT));
  SUB_1 sub_1_2 (.A(in_2[6]), .B(in_1[6]), .Bin(sub_1_3_bout), .S(out_5[6]), .Bout(sub_1_2_bout));
  SUB_1 sub_1_3 (.A(in_2[5]), .B(in_1[5]), .Bin(sub_1_4_bout), .S(out_5[5]), .Bout(sub_1_3_bout));
  SUB_1 sub_1_4 (.A(in_2[4]), .B(in_1[4]), .Bin(sub_1_5_bout), .S(out_5[4]), .Bout(sub_1_4_bout));
  SUB_1 sub_1_5 (.A(in_2[3]), .B(in_1[3]), .Bin(sub_1_6_bout), .S(out_5[3]), .Bout(sub_1_5_bout));
  SUB_1 sub_1_6 (.A(in_2[2]), .B(in_1[2]), .Bin(sub_1_7_bout), .S(out_5[2]), .Bout(sub_1_6_bout));
  SUB_1 sub_1_7 (.A(in_2[1]), .B(in_1[1]), .Bin(sub_1_8_bout), .S(out_5[1]), .Bout(sub_1_7_bout));
  SUB_1 sub_1_8 (.A(in_2[0]), .B(in_1[0]), .Bin(Bin), .S(out_5[0]), .Bout(sub_1_8_bout));
endmodule

module MUX_2_1_1 (
  input  A,
  input  B,
  input  S,
  output M
);

  wire and_1_out, and_2_out, not_1_out;

  not not_1 (not_1_out, S);
  and and_1 (and_1_out, B, S);
  and and_2 (and_2_out, A, not_1_out);
  or or_1 (M, and_1_out, and_2_out);
endmodule

module MUX_4_1_1 (
  input  in_1,
  input  in_2,
  input  in_3,
  input  in_4,
  input  in_5,
  input  in_6,
  output M
);

  wire mux_2_1_1_1_m, mux_2_1_1_2_m;

  MUX_2_1_1 mux_2_1_1_1 (.B(in_2), .M(mux_2_1_1_1_m), .A(in_1), .S(in_5));
  MUX_2_1_1 mux_2_1_1_2 (.B(in_4), .M(mux_2_1_1_2_m), .A(in_3), .S(in_5));
  MUX_2_1_1 mux_2_1_1_3 (.B(mux_2_1_1_2_m), .M(M), .A(mux_2_1_1_1_m), .S(in_6));
endmodule

module MUX_8_1_1 (
  input  A,
  input  B,
  input  C,
  input  D,
  input  E,
  input  F,
  input  G,
  input  H,
  input  S1,
  input  S2,
  input  S3,
  output out_12
);

  wire mux_4_1_1_1_m, mux_4_1_1_2_m;

  MUX_4_1_1 mux_4_1_1_1 (.in_1(A), .in_2(B), .in_3(C), .in_4(D), .M(mux_4_1_1_1_m), .in_5(S1), .in_6(S2));
  MUX_4_1_1 mux_4_1_1_2 (.in_1(E), .in_2(F), .in_3(G), .in_4(H), .M(mux_4_1_1_2_m), .in_5(S1), .in_6(S2));
  MUX_2_1_1 mux_2_1_1_1 (.B(mux_4_1_1_2_m), .M(out_12), .A(mux_4_1_1_1_m), .S(S3));
endmodule

module MUX_2_1_8 (
  input  [7:0] in_1,
  input  [7:0] in_2,
  input  S,
  output [7:0] M
);

  MUX_2_1_1 mux_2_1_1_1 (.B(in_2[0]), .M(M[0]), .A(in_1[0]), .S(S));
  MUX_2_1_1 mux_2_1_1_2 (.B(in_2[1]), .M(M[1]), .A(in_1[1]), .S(S));
  MUX_2_1_1 mux_2_1_1_3 (.B(in_2[2]), .M(M[2]), .A(in_1[2]), .S(S));
  MUX_2_1_1 mux_2_1_1_4 (.B(in_2[3]), .M(M[3]), .A(in_1[3]), .S(S));
  MUX_2_1_1 mux_2_1_1_5 (.B(in_2[4]), .M(M[4]), .A(in_1[4]), .S(S));
  MUX_2_1_1 mux_2_1_1_6 (.B(in_2[5]), .M(M[5]), .A(in_1[5]), .S(S));
  MUX_2_1_1 mux_2_1_1_7 (.B(in_2[6]), .M(M[6]), .A(in_1[6]), .S(S));
  MUX_2_1_1 mux_2_1_1_8 (.B(in_2[7]), .M(M[7]), .A(in_1[7]), .S(S));
endmodule

module MUX_4_1_8 (
  input  [7:0] in_1,
  input  [7:0] in_2,
  input  [7:0] in_3,
  input  [7:0] in_4,
  input  S,
  input  S_2,
  output [7:0] M
);

  wire [7:0] mux_2_1_8_1_m, mux_2_1_8_2_m;

  MUX_2_1_8 mux_2_1_8_1 (.in_1(in_1), .in_2(in_2), .M(mux_2_1_8_1_m), .S(S));
  MUX_2_1_8 mux_2_1_8_2 (.in_1(in_3), .in_2(in_4), .M(mux_2_1_8_2_m), .S(S));
  MUX_2_1_8 mux_2_1_8_3 (.in_1(mux_2_1_8_1_m), .in_2(mux_2_1_8_2_m), .M(M), .S(S_2));
endmodule

module MUX_8_1_8 (
  input  [7:0] in_1,
  input  [7:0] in_2,
  input  [7:0] in_3,
  input  [7:0] in_4,
  input  [7:0] in_5,
  input  [7:0] in_6,
  input  [7:0] in_7,
  input  [7:0] in_8,
  input  S1,
  input  S2,
  input  S3,
  output [7:0] M
);

  wire [7:0] mux_4_1_8_1_m, mux_4_1_8_2_m;

  MUX_4_1_8 mux_4_1_8_1 (.in_1(in_1), .in_2(in_2), .in_3(in_3), .in_4(in_4), .M(mux_4_1_8_1_m), .S(S1), .S_2(S2));
  MUX_4_1_8 mux_4_1_8_2 (.in_1(in_5), .in_2(in_6), .in_3(in_7), .in_4(in_8), .M(mux_4_1_8_2_m), .S(S1), .S_2(S2));
  MUX_2_1_8 mux_2_1_8_1 (.in_1(mux_4_1_8_1_m), .in_2(mux_4_1_8_2_m), .M(M), .S(S3));
endmodule

module AND_8 (
  input  [7:0] in_1,
  input  [7:0] in_2,
  output [7:0] out_3
);

  and and_1 (out_3[7], in_1[7], in_2[7]);
  and and_2 (out_3[6], in_1[6], in_2[6]);
  and and_3 (out_3[5], in_1[5], in_2[5]);
  and and_4 (out_3[4], in_1[4], in_2[4]);
  and and_5 (out_3[3], in_1[3], in_2[3]);
  and and_6 (out_3[2], in_1[2], in_2[2]);
  and and_7 (out_3[1], in_1[1], in_2[1]);
  and and_8 (out_3[0], in_1[0], in_2[0]);
endmodule

module OR_8 (
  input  [7:0] in_1,
  input  [7:0] in_2,
  output [7:0] out_3
);

  or or_1 (out_3[7], in_1[7], in_2[7]);
  or or_2 (out_3[6], in_1[6], in_2[6]);
  or or_3 (out_3[5], in_1[5], in_2[5]);
  or or_4 (out_3[4], in_1[4], in_2[4]);
  or or_5 (out_3[2], in_1[2], in_2[2]);
  or or_6 (out_3[3], in_1[3], in_2[3]);
  or or_7 (out_3[1], in_1[1], in_2[1]);
  or or_8 (out_3[0], in_1[0], in_2[0]);
endmodule

module XOR_8 (
  input  [7:0] in_1,
  input  [7:0] in_2,
  output [7:0] out_3
);

  xor xor_1 (out_3[7], in_1[7], in_2[7]);
  xor xor_2 (out_3[6], in_1[6], in_2[6]);
  xor xor_3 (out_3[5], in_1[5], in_2[5]);
  xor xor_4 (out_3[4], in_1[4], in_2[4]);
  xor xor_5 (out_3[3], in_1[3], in_2[3]);
  xor xor_6 (out_3[2], in_1[2], in_2[2]);
  xor xor_7 (out_3[1], in_1[1], in_2[1]);
  xor xor_8 (out_3[0], in_1[0], in_2[0]);
endmodule

module SHR_8 (
  input  [7:0] in_1,
  input  Cin,
  output [7:0] SHIFT_RIGHT__X1_2,
  output Cout
);


  assign Cout = in_1[0];
  assign SHIFT_RIGHT__X1_2 = {Cin, in_1[7:1]};
endmodule

module SHL_8 (
  input  Cin,
  input  [7:0] in_2,
  output [7:0] SHIFT_LEFT__X2,
  output Cout
);


  assign Cout = in_2[7];
  assign SHIFT_LEFT__X2 = {in_2[6:0], Cin};
endmodule

module ZERO (
  input  [7:0] in_1,
  output Z
);

  wire or_1_out, or_2_out, or_3_out, or_4_out, or_5_out, or_6_out, or_7_out;

  or or_1 (or_1_out, in_1[3], in_1[7]);
  or or_2 (or_2_out, or_1_out, or_3_out);
  or or_3 (or_3_out, in_1[2], in_1[6]);
  or or_4 (or_4_out, or_2_out, or_7_out);
  not not_1 (Z, or_4_out);
  or or_5 (or_5_out, in_1[0], in_1[4]);
  or or_6 (or_6_out, in_1[1], in_1[5]);
  or or_7 (or_7_out, or_6_out, or_5_out);
endmodule

module DEC_16DISPLAY7 (
  input  A,
  input  B,
  input  C,
  input  D,
  output a_2,
  output b_2,
  output c_2,
  output d_2,
  output e,
  output f,
  output g,
  output out_12
);

  wire and_1_out, and_2_out, and_3_out, and_4_out, and_5_out, and_6_out, and_7_out, and_8_out, and_9_out,
       and_10_out, and_11_out, and_12_out, and_13_out, and_14_out, and_15_out, and_16_out, and_17_out,
       and_18_out, and_19_out, and_20_out, and_21_out, and_22_out, and_23_out, and_24_out, and_25_out,
       and_26_out, and_27_out, and_28_out, and_29_out, and_30_out, and_31_out, and_32_out, and_33_out,
       and_34_out, and_35_out, and_36_out, not_1_out, not_2_out, not_3_out, not_4_out, not_5_out, not_6_out,
       not_7_out, not_8_out, not_9_out, not_10_out, not_11_out, not_12_out, not_13_out, not_14_out,
       not_15_out, not_16_out, not_17_out, not_18_out, not_19_out, not_20_out, not_21_out, not_22_out,
       not_23_out, not_24_out, not_25_out, not_26_out, not_27_out, not_28_out, not_29_out, not_30_out,
       not_31_out, not_32_out, not_33_out, not_34_out, not_35_out, not_36_out, not_37_out, not_38_out,
       not_39_out, not_40_out, not_41_out, not_42_out, not_43_out, not_44_out, not_45_out;

  not not_1 (not_1_out, B);
  and and_1 (and_1_out, not_1_out, not_2_out);
  not not_2 (not_2_out, D);
  not not_3 (not_3_out, A);
  and and_2 (and_2_out, not_3_out, C);
  not not_4 (not_4_out, A);
  and and_3 (and_3_out, not_4_out, B, D);
  and and_4 (and_4_out, B, C);
  not not_5 (not_5_out, B);
  and and_5 (and_5_out, A, not_5_out, not_6_out);
  not not_6 (not_6_out, C);
  and and_6 (and_6_out, A, not_7_out);
  not not_7 (not_7_out, D);
  not not_8 (not_8_out, A);
  and and_7 (and_7_out, not_8_out, not_9_out);
  not not_9 (not_9_out, B);
  not not_10 (not_10_out, A);
  and and_8 (and_8_out, not_10_out, not_11_out, not_12_out);
  not not_11 (not_11_out, C);
  not not_12 (not_12_out, D);
  not not_13 (not_13_out, B);
  and and_9 (and_9_out, not_13_out, not_14_out);
  not not_14 (not_14_out, C);
  not not_15 (not_15_out, B);
  and and_10 (and_10_out, not_15_out, not_16_out);
  not not_16 (not_16_out, D);
  not not_17 (not_17_out, A);
  and and_11 (and_11_out, not_17_out, C, D);
  and and_12 (and_12_out, A, not_18_out, D);
  not not_18 (not_18_out, C);
  not not_19 (not_19_out, A);
  and and_13 (and_13_out, not_19_out, not_20_out);
  not not_20 (not_20_out, C);
  not not_21 (not_21_out, A);
  and and_14 (and_14_out, not_21_out, D);
  not not_22 (not_22_out, C);
  and and_15 (and_15_out, not_22_out, D);
  not not_23 (not_23_out, A);
  and and_16 (and_16_out, not_23_out, B);
  and and_17 (and_17_out, A, not_24_out);
  not not_24 (not_24_out, B);
  not not_25 (not_25_out, A);
  and and_18 (and_18_out, not_25_out, not_26_out, not_27_out);
  not not_26 (not_26_out, B);
  not not_27 (not_27_out, D);
  not not_28 (not_28_out, B);
  and and_19 (and_19_out, not_28_out, C, D);
  not not_29 (not_29_out, C);
  and and_20 (and_20_out, B, not_29_out, D);
  and and_21 (and_21_out, B, C, not_30_out);
  not not_30 (not_30_out, D);
  and and_22 (and_22_out, A, not_31_out);
  not not_31 (not_31_out, C);
  not not_32 (not_32_out, B);
  and and_23 (and_23_out, not_32_out, not_33_out);
  not not_33 (not_33_out, D);
  and and_24 (and_24_out, C, not_34_out);
  not not_34 (not_34_out, D);
  and and_25 (and_25_out, A, C);
  and and_26 (and_26_out, A, B);
  not not_35 (not_35_out, C);
  and and_27 (and_27_out, not_35_out, not_36_out);
  not not_36 (not_36_out, D);
  not not_37 (not_37_out, A);
  and and_28 (and_28_out, not_37_out, B, not_38_out);
  not not_38 (not_38_out, C);
  and and_29 (and_29_out, B, not_39_out);
  not not_39 (not_39_out, D);
  and and_30 (and_30_out, A, not_40_out);
  not not_40 (not_40_out, B);
  and and_31 (and_31_out, A, C);
  not not_41 (not_41_out, B);
  and and_32 (and_32_out, not_41_out, C);
  and and_33 (and_33_out, C, not_42_out);
  not not_42 (not_42_out, D);
  not not_43 (not_43_out, A);
  and and_34 (and_34_out, not_43_out, B, not_44_out);
  not not_44 (not_44_out, C);
  and and_35 (and_35_out, A, not_45_out);
  not not_45 (not_45_out, B);
  and and_36 (and_36_out, A, D);
  or or_1 (c_2, and_13_out, and_14_out, and_15_out, and_16_out, and_17_out);
  or or_2 (d_2, and_18_out, and_19_out, and_20_out, and_21_out, and_22_out);
  or or_3 (e, and_23_out, and_24_out, and_25_out, and_26_out);
  or or_4 (f, and_27_out, and_28_out, and_29_out, and_30_out, and_31_out);
  or or_5 (g, and_32_out, and_33_out, and_34_out, and_35_out, and_36_out);
  or or_6 (a_2, and_1_out, and_2_out, and_3_out, and_4_out, and_5_out, and_6_out);
  or or_7 (b_2, and_7_out, and_8_out, and_9_out, and_10_out, and_11_out, and_12_out);

  assign out_12 = 1'b0;
endmodule

module Calculadora (
  input  Cin,
  input  [7:0] A,
  input  [7:0] B,
  input  [2:0] OP,
  output Z,
  output C
);

  wire dec_16display7_1_a_2, dec_16display7_1_b_2, dec_16display7_1_c_2, dec_16display7_1_d_2,
       dec_16display7_1_e, dec_16display7_1_f, dec_16display7_1_g, dec_16display7_1_out_12,
       dec_16display7_2_a_2, dec_16display7_2_b_2, dec_16display7_2_c_2, dec_16display7_2_d_2,
       dec_16display7_2_e, dec_16display7_2_f, dec_16display7_2_g, dec_16display7_2_out_12;
  wire [7:0] alu_8_1_s;

  ALU_8 alu_8_1 (.A(A), .B(B), .Z(Z), .S(alu_8_1_s), .C(C), .Cin(Cin), .OP(OP));
  DEC_16DISPLAY7 dec_16display7_1 (
    .A(alu_8_1_s[7]), .B(alu_8_1_s[6]), .C(alu_8_1_s[5]), .D(alu_8_1_s[4]), .a_2(dec_16display7_1_a_2),
    .b_2(dec_16display7_1_b_2), .c_2(dec_16display7_1_c_2), .d_2(dec_16display7_1_d_2),
    .e(dec_16display7_1_e), .f(dec_16display7_1_f), .g(dec_16display7_1_g), .out_12(dec_16display7_1_out_12));
  DEC_16DISPLAY7 dec_16display7_2 (
    .A(alu_8_1_s[3]), .B(alu_8_1_s[2]), .C(alu_8_1_s[1]), .D(alu_8_1_s[0]), .a_2(dec_16display7_2_a_2),
    .b_2(dec_16display7_2_b_2), .c_2(dec_16display7_2_c_2), .d_2(dec_16display7_2_d_2),
    .e(dec_16display7_2_e), .f(dec_16display7_2_f), .g(dec_16display7_2_g), .out_12(dec_16display7_2_out_12));
  _7_Segment_Display u_7_segment_display_1 (
    .g(dec_16display7_1_g), .f(dec_16display7_1_f), .a(dec_16display7_1_a_2), .b(dec_16display7_1_b_2),
    .e(dec_16display7_1_e), .d(dec_16display7_1_d_2), .c(dec_16display7_1_c_2), .dp(dec_16display7_1_out_12));
  _7_Segment_Display u_7_segment_display_2 (
    .g(dec_16display7_2_g), .f(dec_16display7_2_f), .a(dec_16display7_2_a_2), .b(dec_16display7_2_b_2),
    .e(dec_16display7_2_e), .d(dec_16display7_2_d_2), .c(dec_16display7_2_c_2), .dp(dec_16display7_2_out_12));
endmodule

module VALIDA_COUT (
  input  A,
  input  B,
  input  C,
  output S
);

  wire and_1_out, and_2_out, and_3_out, not_1_out, not_2_out, not_3_out, not_4_out;

  not not_1 (not_1_out, A);
  not not_2 (not_2_out, B);
  not not_3 (not_3_out, B);
  not not_4 (not_4_out, C);
  and and_1 (and_1_out, not_1_out, not_2_out);
  and and_2 (and_2_out, not_3_out, C);
  and and_3 (and_3_out, A, B, not_4_out);
  or or_1 (S, and_1_out, and_2_out, and_3_out);
endmodule

module CARRY_SHR (
  input  [7:0] in_1,
  output S
);


  assign S = in_1[0];
endmodule

module CARRY_SHL (
  input  [7:0] in_1,
  output S
);


  assign S = in_1[7];
endmodule

module OP__ADD (
  input  [2:0] in_1,
  output S
);

  wire not_1_out, not_2_out, not_3_out;

  not not_1 (not_1_out, in_1[0]);
  not not_2 (not_2_out, in_1[1]);
  not not_3 (not_3_out, in_1[2]);
  and and_1 (S, not_1_out, not_2_out, not_3_out);
endmodule

module OP__SUB (
  input  [2:0] in_1,
  output S
);

  wire not_1_out, not_2_out;

  not not_1 (not_1_out, in_1[1]);
  not not_2 (not_2_out, in_1[2]);
  and and_1 (S, in_1[0], not_1_out, not_2_out);
endmodule

module VALIDA_COUTS (
  input  Cout0,
  input  Cout1,
  input  [7:0] A1,
  input  [7:0] A0,
  input  [2:0] OP,
  output Cout
);

  wire and_1_out, and_2_out, and_3_out, and_4_out, carry_shl_1_s, carry_shr_1_s, op_add_1_s, op_sub_1_s,
       or_1_out, or_2_out;

  CARRY_SHR carry_shr_1 (.in_1(A1), .S(carry_shr_1_s));
  CARRY_SHL carry_shl_1 (.in_1(A0), .S(carry_shl_1_s));
  OP__SUB op_sub_1 (.in_1(OP), .S(op_sub_1_s));
  OP__ADD op_add_1 (.in_1(OP), .S(op_add_1_s));
  and and_1 (and_1_out, Cout1, carry_shr_1_s);
  and and_2 (and_2_out, Cout0, carry_shl_1_s);
  and and_3 (and_3_out, Cout0, op_sub_1_s);
  and and_4 (and_4_out, Cout0, op_add_1_s);
  or or_1 (or_1_out, and_1_out, and_2_out);
  or or_2 (or_2_out, and_3_out, and_4_out);
  or or_3 (Cout, or_1_out, or_2_out);
endmodule

module VALIDA_CINS (
  input  [7:0] A0,
  input  [2:0] OP,
  input  Cout0,
  input  Cin,
  output Cout
);

  wire and_1_out, and_2_out, carry_shl_1_s, not_1_out, not_2_out, op_add_1_s;

  CARRY_SHL carry_shl_1 (.in_1(A0), .S(carry_shl_1_s));
  not not_1 (not_1_out, carry_shl_1_s);
  not not_2 (not_2_out, op_add_1_s);
  OP__ADD op_add_1 (.in_1(OP), .S(op_add_1_s));
  and and_1 (and_1_out, not_2_out, Cout0);
  and and_2 (and_2_out, and_1_out, not_1_out);
  or or_1 (Cout, and_2_out, Cin);
endmodule
